# Fritzing sketch NodeMCU - Emitir Comandos (saved by Fritzing 0.9.3b)
breadboards: 1

parts:
  NodeMCU_v1 = NodeMCU v3 LoLin [part_number=ESP8266]
  R1 = Resistor [tolerance=±5% resistance=1k package="0603 [SMD]"]
  Q1 = NPN-Transistor [package="TO92 [THT]"]
  R2 = Resistor [tolerance=±5% resistance=470 package="0603 [SMD]"]
  LED1 = LED - 3mm [color="Infrared (940nm)" package="3 mm [THT]"]

nets:
  N1: NodeMCU_v1.D2, R1.Pin_1
  N2: NodeMCU_v1.GND, Q1.C
  N3: NodeMCU_v1.VU, LED1.anode
  N4: R1.Pin_0, Q1.B
  N5: Q1.E, R2.Pin_0
  N6: R2.Pin_1, LED1.cathode

custom parts:
  NodeMCU v3 LoLin: NodeMCU v3 LoLin NodeMCU (http://www.nodemcu.com/) is an open source IoT platform. It includes firmware (https://nodemcu-build.com/) which runs on the ESP8266 Wi-Fi SoC from Espressif Systems, and hardware which is based on the ESP-12E module. The term "NodeMCU" by default refers to the firmware rather than the dev kits. The firmware uses the Lua scripting language. It is based on the eLua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
